# Fritzing sketch TwinUltrasonicSensors-ArduEV3overI2C (saved by Fritzing 0.9.3b)
breadboards: 1

parts:
  Part1 = Arduino Uno (Rev3)
  J1 = RJ11 Jack [package=rj11-6]
  hc-sr1 = hc-sr04
  hc-sr2 = hc-sr04
  R1 = Resistor [tolerance=±5% resistance=4.7k package=THT]
  R2 = Resistor [tolerance=±5% resistance=4.7k package=THT]

nets:
  N1: Part1.A4/SDA, J1.6, R2.Pin_0
  N2: Part1.A5/SCL, J1.5, R1.Pin_0
  N3: Part1.D11_PWM/MOSI, hc-sr1.Echo
  N4: Part1.D12/MISO, hc-sr1.Trig
  N5: Part1.D2, hc-sr2.Echo
  N6: Part1.D3_PWM, hc-sr2.Trig
  GND: Part1.GND, J1.2, hc-sr1.GND
  VIN: Part1.VIN, J1.4, hc-sr1.VCC, R1.Pin_1, R2.Pin_1
  N7: J1.3, hc-sr2.GND

// code stored in the sketch: I2CArduino-EV3-twin_ultrasonic.ino
#include <NewPing.h>
#include <Wire.h>

#define SLAVE_ADDRESS 0x04 //0x04 
#define TRIGGER_PIN  12
#define ECHO_PIN     11
#define MAX_DISTANCE 200
 
NewPing sonar1(TRIGGER_PIN, ECHO_PIN);
NewPing sonar2(3, 2);
int uS1, uS2;
String dist,dist1,dist2;
int val,flag=0,index=0;
unsigned char buf[8];
void setup() 
{
  Serial.begin(9600);
  Wire.begin(SLAVE_ADDRESS);
    Wire.onReceive(receiveData);
    Wire.onRequest(sendData);
}
 
void loop() 
{
  
 // if(flag!=1)
  //{
    uS1 = sonar1.ping();
    uS2 = sonar2.ping();
  //Serial.print("Ping: ");
  //Serial.print(uS1 / US_ROUNDTRIP_CM);
    dist1=(String)(uS1 / US_ROUNDTRIP_CM);
   //Serial.print(" ");
  //Serial.print(dist1.length());
  //Serial.print(" ");
  //Serial.print(uS2 / US_ROUNDTRIP_CM);
    dist2=(String)(uS2 / US_ROUNDTRIP_CM);
   //Serial.print(" ");
  //Serial.print(dist2.length());
    dist=dist1+" "+dist2;
  /*
   * Serial.print(dist1);
  Serial.print(" ");
  Serial.print(dist1.length());
  Serial.println();
  Serial.println("cm");
  */
  dist.toCharArray(buf,8);
 // }
 delay(50);
}

void receiveData(int byteCount)
{
    while(Wire.available()>0) 
    {
      val=Wire.read();
      //Serial.print((char)val);
      flag=1;
    }
}

// callback for sending data
void sendData()
{
  
  Wire.write(buf,8);
  //Wire.write(dist[1]);
}
